// Logisim project logic project.circ as structural Verilog: 1 circuit, main circuit main
module main (
  input  x3,
  input  x2,
  input  x1,
  input  x0,
  input  [1:0] in_5,
  input  in_6,
  output out_7,
  output out_8,
  output out_9,
  output out_10
);

  wire clock_1_out, d_ff_1_qn, d_ff_2_qn, d_ff_3_qn, d_ff_4_qn, multiplexer_1_out, multiplexer_2_out,
       multiplexer_3_out, multiplexer_4_out;

  Multiplexer #(.select(2)) multiplexer_1 (
    .in0(x3), .in1(out_8), .in2(out_10), .in3(x0), .out(multiplexer_1_out), .sel(in_5), .en(in_6));
  Multiplexer #(.select(2)) multiplexer_2 (
    .in0(x2), .in1(out_9), .in2(x0), .in3(out_8), .out(multiplexer_2_out), .sel(in_5), .en(in_6));
  Multiplexer #(.select(2)) multiplexer_3 (
    .in0(x1), .in1(out_10), .in2(out_8), .in3(out_9), .out(multiplexer_3_out), .sel(in_5), .en(in_6));
  Multiplexer #(.select(2)) multiplexer_4 (
    .in0(x0), .in1(x0), .in2(out_9), .in3(out_10), .out(multiplexer_4_out), .sel(in_5), .en(in_6));
  Clock clock_1 (.out(clock_1_out));
  D_Flip_Flop d_ff_1 (.clk(clock_1_out), .D(multiplexer_1_out), .Q(x0), .Qn(d_ff_1_qn));  // open: preset, en, reset
  D_Flip_Flop d_ff_2 (.clk(clock_1_out), .D(multiplexer_2_out), .Q(out_8), .Qn(d_ff_2_qn));  // open: preset, en, reset
  D_Flip_Flop d_ff_3 (.clk(clock_1_out), .D(multiplexer_3_out), .Q(out_9), .Qn(d_ff_3_qn));  // open: preset, en, reset
  D_Flip_Flop d_ff_4 (.clk(clock_1_out), .D(multiplexer_4_out), .Q(out_10), .Qn(d_ff_4_qn));  // open: preset, en, reset

  assign out_7 = x0;
endmodule
